# Fritzing sketch fritzing (saved by Fritzing 0.9.2b)

parts:
  Part2 = Arduino Ethernet Shield (Rev3)
  Eleman4 = RFID-RC522-v2
  R1 = Resistor [tolerance=±5% resistance=220 package="0805 [SMD]"]
  LED1 = LED - 3mm [color="Green (555nm)" package="3 mm [THT]"]

nets:
  N1: Part2.PWM_D11, Eleman4.MOSI
  N2: Part2.SPI/D12, Eleman4.MISO
  N3: Part2.SPI/D13, Eleman4.SCK
  GND: Part2.GND, Eleman4.GND, LED1.cathode
  N4: Part2.PWM_D5, R1.Pin_1
  N5: Part2.PWM_D6, Eleman4.RST
  N6: Part2.D7, Eleman4.SDA
  3V3: Part2.3V3, Eleman4.3.3V
  N7: R1.Pin_0, LED1.anode

custom parts:
  RFID-RC522-v2: A simple China made RFID-RC522 Reader; do check the pin labels, as this is a MFRC522 based clone.
